// Logisim project MIC-1.circ as structural Verilog: 28 circuits, main circuit main
module main (
  input  CLK,
  output [31:0] PC,
  output [8:0] MPC,
  output [31:0] B,
  output [31:0] C
);

  wire data_path_1_p8, data_path_1_p9, data_path_1_p10, data_path_1_p11, data_path_1_p12, data_path_1_p13,
       data_path_1_p14, data_path_1_p15, data_path_1_p16, data_path_1_p24, data_path_1_p25, data_path_1_p26,
       data_path_1_p27, data_path_1_p28, data_path_1_p29, data_path_1_p30, data_path_1_p31, data_path_1_p32,
       data_path_1_p34, data_path_1_p35, RESET_out;
  wire [1:0] data_path_1_p21, data_path_1_p38;
  wire [2:0] data_path_1_p7;
  wire [3:0] data_path_1_p17;
  wire [7:0] data_path_1_p33, mem_1_mem_fetch;
  wire [31:0] data_path_1_p1, data_path_1_p2, mem_1_mrm_rd;

  Mem mem_1 (
    .MEM_ADDR_32(data_path_1_p1), .CLK(CLK), .MEM_WR(data_path_1_p2), .MRM_RD(mem_1_mrm_rd),
    .MEM_FETCH(mem_1_mem_fetch), .wr(data_path_1_p7[2]), .rd(data_path_1_p7[1]), .fetch(data_path_1_p7[0]),
    .MEM_ADDR_8(PC));
  Button RESET (.out(RESET_out));
  // Data_Path data_path_1: pin names not known; wires that end beside it: data_path_1_p1, data_path_1_p2, mem_1_mrm_rd, data_path_1_p7[1], PC, mem_1_mem_fetch, data_path_1_p7[0], data_path_1_p8, data_path_1_p9, data_path_1_p10, data_path_1_p11, data_path_1_p12, data_path_1_p13, data_path_1_p14, data_path_1_p15, data_path_1_p16, data_path_1_p17[0], data_path_1_p17[1], data_path_1_p17[2], data_path_1_p17[3], data_path_1_p21, CLK, RESET_out, data_path_1_p24, data_path_1_p25, data_path_1_p26, data_path_1_p27, data_path_1_p28, data_path_1_p29, data_path_1_p30, data_path_1_p31, data_path_1_p32, data_path_1_p33, data_path_1_p34, data_path_1_p35, B, C, data_path_1_p38[0], data_path_1_p38[1]
  Control_Unit control_unit_1 (
    .CLK(CLK), .RESET(RESET_out), .MBR(data_path_1_p33), .N(data_path_1_p34), .Z(data_path_1_p35), .MPC(MPC),
    .MDR_B(data_path_1_p24), .PC_B(data_path_1_p25), .MBR_B(data_path_1_p26), .MBRU_B(data_path_1_p27),
    .SP_B(data_path_1_p28), .LV_B(data_path_1_p29), .CPP_B(data_path_1_p30), .TOS_B(data_path_1_p31),
    .OPC_B(data_path_1_p32), .Mem(data_path_1_p7), .ALU({data_path_1_p21, data_path_1_p17}),
    .Shifter(data_path_1_p38), .H_C(data_path_1_p16), .OPC_C(data_path_1_p15), .TOS_C(data_path_1_p14),
    .CPP_C(data_path_1_p13), .LV_C(data_path_1_p12), .SP_C(data_path_1_p11), .PC_C(data_path_1_p10),
    .MDR_C(data_path_1_p9), .MAR_C(data_path_1_p8));
endmodule

module Mem (
  input  wr,
  input  [31:0] MEM_WR,
  input  [31:0] MEM_ADDR_32,
  input  rd,
  input  [31:0] MEM_ADDR_8,
  input  fetch,
  input  CLK,
  output [31:0] MRM_RD,
  output [7:0] MEM_FETCH
);

  wire not_1_out, not_2_out, not_3_out;
  wire [7:0] ram_2_data;
  wire [31:0] ram_1_data;

  not not_1 (not_1_out, CLK);
  not not_2 (not_2_out, wr);
  RAM #(.addrWidth(24), .dataWidth(32)) ram_1 (
    .addr(MEM_ADDR_32[23:0]), .data(ram_1_data), .sel(1'b1), .clk(not_1_out), .ld(not_2_out), .clr(1'b0));
  assign ram_1_data = wr ? MEM_WR : 32'bz;  // Controlled_Buffer controlled_buffer_1
  assign MRM_RD = rd ? ram_1_data : 32'bz;  // Controlled_Buffer controlled_buffer_2
  not not_3 (not_3_out, CLK);
  assign MEM_FETCH = fetch ? ram_2_data : 8'bz;  // Controlled_Buffer controlled_buffer_3
  RAM #(.addrWidth(24)) ram_2 (
    .addr(MEM_ADDR_8[23:0]), .data(ram_2_data), .sel(1'b1), .clk(not_3_out), .clr(1'b0));  // open: ld

  // Notes on the sheet:
  //   Una truchada porque Logisim no tiene
  //   un bloque de memoria con dos canales de datos
endmodule

module Control_Unit (
  input  CLK,
  input  RESET,
  input  [7:0] MBR,
  input  N,
  input  Z,
  output [8:0] MPC,
  output MDR_B,
  output PC_B,
  output MBR_B,
  output MBRU_B,
  output SP_B,
  output LV_B,
  output CPP_B,
  output TOS_B,
  output OPC_B,
  output [2:0] Mem,
  output [5:0] ALU,
  output [1:0] Shifter,
  output H_C,
  output OPC_C,
  output TOS_C,
  output CPP_C,
  output LV_C,
  output SP_C,
  output PC_C,
  output MDR_C,
  output MAR_C
);

  wire and_1_out, and_2_out, d_flipflop_asc_1_p4, d_flipflop_asc_1_p5, d_flipflop_asc_2_p5;
  wire [2:0] mir_1_jam;
  wire [3:0] control_store_1_cs_s4, mir_1_b;
  wire [7:0] mir_1_addr, multiplexer_3_out, or_2_out;
  wire [8:0] multiplexer_1_out, multiplexer_2_out;
  wire [8:8] mir_1_addr_2, or_1_out;
  wire [31:0] control_store_1_cs_s32;

  Multiplexer #(.width(9), .enable("false")) multiplexer_1 (
    .in0({9{1'b1}}), .in1(9'hff), .out(multiplexer_1_out), .sel(RESET));
  Multiplexer #(.width(9), .enable("false")) multiplexer_2 (
    .in0({9{1'b1}}), .in1(9'h100), .out(multiplexer_2_out), .sel(RESET));
  and and_1 (and_1_out, d_flipflop_asc_1_p5, mir_1_jam[1]);
  // D_FlipFlop_Asc d_flipflop_asc_1: pin names not known; wires that end beside it: N, CLK, 1'b1, d_flipflop_asc_1_p4, d_flipflop_asc_1_p5
  // D_FlipFlop_Asc d_flipflop_asc_2: pin names not known; wires that end beside it: Z, CLK, 1'b1, d_flipflop_asc_1_p4, d_flipflop_asc_2_p5
  Multiplexer #(.width(8), .enable("false")) multiplexer_3 (
    .in0(mir_1_addr), .in1(or_2_out), .out(multiplexer_3_out), .sel(mir_1_jam[2]));
  or or_1 (or_1_out[8], and_1_out, and_2_out, mir_1_addr_2[8]);
  and and_2 (and_2_out, d_flipflop_asc_2_p5, mir_1_jam[0]);
  assign or_2_out = MBR | mir_1_addr;  // OR_Gate or_2, 8 bits wide
  not not_1 (d_flipflop_asc_1_p4, RESET);
  MPC mpc_1 (
    .Entrada({or_1_out[8], multiplexer_3_out}), .CLK(CLK), .Salida(MPC), .nPRE(multiplexer_1_out),
    .nCLR(multiplexer_2_out));
  Control_Store control_store_1 (.CS_E(MPC), .CS_S32(control_store_1_cs_s32), .CS_S4(control_store_1_cs_s4));
  MIR mir_1 (
    .Entrada_4(control_store_1_cs_s4), .Entrada_32(control_store_1_cs_s32), .CLK(CLK), .RESET(RESET),
    .B(mir_1_b), .Mem(Mem), .C({H_C, OPC_C, TOS_C, CPP_C, LV_C, SP_C, PC_C, MDR_C, MAR_C}),
    .ALU({Shifter, ALU}), .JAM(mir_1_jam), .Addr({mir_1_addr_2[8], mir_1_addr}));
  Decoder #(.select(4), .enable("false")) decoder_1 (
    .out0(MDR_B), .out1(PC_B), .out2(MBR_B), .out3(MBRU_B), .out4(SP_B), .out5(LV_B), .out6(CPP_B),
    .out7(TOS_B), .out8(OPC_B), .sel(mir_1_b));  // open: out9, out10, out11, out12, out13, out14, out15
endmodule

module Control_Store (
  input  [8:0] CS_E,
  output [31:0] CS_S32,
  output [3:0] CS_S4
);

  ROM #(.addrWidth(9), .dataWidth(32)) rom_1 (.addr(CS_E), .data(CS_S32), .sel(1'b1));
  ROM #(.addrWidth(9), .dataWidth(4)) rom_2 (.addr(CS_E), .data(CS_S4), .sel(1'b1));

  // Notes on the sheet:
  //   Otra truchada porque Logisim no tiene
  //   un bloque de memoria mas ancho que 32 bits
  //   contents of rom_1 (hex, n*v repeats v):
  //   80000000 255*0 435021
  //   contents of rom_2 (hex, n*v repeats v):
  //   f 255*0 1
endmodule

module MPC (
  input  [8:0] nPRE,
  input  [8:0] Entrada,
  input  CLK,
  input  [8:0] nCLR,
  output [8:0] Salida
);

  // D_Latch d_latch_1: pin names not known; wires that end beside it: Entrada[8], CLK, nPRE[8], nCLR[8], Salida[8]
  // D_Latch d_latch_2: pin names not known; wires that end beside it: Entrada[7], CLK, nPRE[7], nCLR[7], Salida[7]
  // D_Latch d_latch_3: pin names not known; wires that end beside it: Entrada[6], CLK, nPRE[6], nCLR[6], Salida[6]
  // D_Latch d_latch_4: pin names not known; wires that end beside it: Entrada[5], CLK, nPRE[5], nCLR[5], Salida[5]
  // D_Latch d_latch_5: pin names not known; wires that end beside it: Entrada[4], CLK, nPRE[4], nCLR[4], Salida[4]
  // D_Latch d_latch_6: pin names not known; wires that end beside it: Entrada[3], CLK, nPRE[3], nCLR[3], Salida[3]
  // D_Latch d_latch_7: pin names not known; wires that end beside it: Entrada[2], CLK, nPRE[2], nCLR[2], Salida[2]
  // D_Latch d_latch_8: pin names not known; wires that end beside it: Entrada[1], CLK, nPRE[1], nCLR[1], Salida[1]
  // D_Latch d_latch_9: pin names not known; wires that end beside it: Entrada[0], CLK, nPRE[0], nCLR[0], Salida[0]
endmodule

module MIR (
  input  [3:0] Entrada_4,
  input  [31:0] Entrada_32,
  input  CLK,
  input  RESET,
  output [3:0] B,
  output [2:0] Mem,
  output [8:0] C,
  output [7:0] ALU,
  output [2:0] JAM,
  output [8:0] Addr
);

  wire [3:0] multiplexer_2_out, multiplexer_4_out, not_2_out;
  wire [31:0] multiplexer_1_out, multiplexer_3_out, not_1_out;

  Multiplexer #(.width(32), .enable("false")) multiplexer_1 (
    .in0({32{1'b1}}), .in1(not_1_out), .out(multiplexer_1_out), .sel(RESET));
  assign not_1_out = ~32'h435021;  // NOT_Gate not_1, 32 bits wide
  assign not_2_out = ~4'b0001;  // NOT_Gate not_2, 4 bits wide
  Multiplexer #(.width(4), .enable("false")) multiplexer_2 (
    .in0(4'b1111), .in1(not_2_out), .out(multiplexer_2_out), .sel(RESET));
  Multiplexer #(.width(32), .enable("false")) multiplexer_3 (
    .in0({32{1'b1}}), .in1(32'h435021), .out(multiplexer_3_out), .sel(RESET));
  Multiplexer #(.width(4), .enable("false")) multiplexer_4 (
    .in0(4'b1111), .in1(4'b0001), .out(multiplexer_4_out), .sel(RESET));
  Register_32_bits_Des register_32_bits_des_1 (
    .Entrada(Entrada_32), .CLK(CLK), .Salida({Addr, JAM, ALU, C, Mem}), .nPRE(multiplexer_1_out),
    .nCLR(multiplexer_3_out));
  Register_4_bits_Des register_4_bits_des_1 (
    .Entrada(Entrada_4), .CLK(CLK), .Salida(B), .nPRE(multiplexer_2_out), .nCLR(multiplexer_4_out));
endmodule

module Data_Path (
  input  MAR_C,
  input  [31:0] MEM_RD,
  input  MDR_C,
  input  rd,
  input  MDR_B,
  input  PC_C,
  input  [7:0] MEM_FETCH,
  input  PC_B,
  input  MBR_C,
  input  MBR,
  input  MBRU,
  input  fetch,
  input  SP_C,
  input  SP_B,
  input  LV_C,
  input  LV_B,
  input  CPP_C,
  input  CPP_B,
  input  RESET,
  input  TOS_C,
  input  TOS_B,
  input  OPC_C,
  input  OPC_B,
  input  H_C,
  input  INC,
  input  INVA,
  input  CLK,
  input  ENA,
  input  ENB,
  input  [1:0] F,
  input  SRA1,
  input  SLL8,
  output [31:0] MEM_WR,
  output [31:0] MEM_MAR,
  output [31:0] MEM_PC,
  output [7:0] OP_CODE
);

  wire [7:0] multiplexer_1_out, register_8_bits_hold_paralel_load_2_salida,
       register_32_bits_hold_paralel_load_4_salida, register_32_bits_hold_paralel_load_4_salida_2,
       register_32_bits_hold_paralel_load_4_salida_3;
  wire [31:0] alu_32_bit_1_p9, multiplexer_2_out, multiplexer_3_out,
       register_32_bits_hold_paralel_load_2_salida, register_32_bits_hold_paralel_load_5_p2,
       register_32_bits_hold_paralel_load_5_p6, register_32_bits_hold_paralel_load_6_salida,
       register_32_bits_hold_paralel_load_7_p6, register_32_bits_hold_paralel_load_8_salida,
       register_32_bits_hold_paralel_load_9_salida, register_32_bits_hold_paralel_load_10_salida;
  wire [31:30] register_32_bits_hold_paralel_load_1_salida;

  Multiplexer #(.width(8), .enable("false")) multiplexer_1 (
    .in0({8{1'b1}}), .in1({8{1'b0}}), .out(multiplexer_1_out), .sel(RESET));
  Multiplexer #(.width(32), .enable("false")) multiplexer_2 (
    .in0({32{1'b1}}), .in1({32{1'b0}}), .out(multiplexer_2_out), .sel(RESET));
  Multiplexer #(.width(32), .enable("false")) multiplexer_3 (
    .in0(register_32_bits_hold_paralel_load_5_p2), .in1(MEM_RD), .out(multiplexer_3_out), .sel(rd));
  // Register_8_bits_Hold___Paralel_Load register_8_bits_hold_paralel_load_1: pin names not known; wires that end beside it: MEM_FETCH, fetch, CLK, {8{1'b1}}, multiplexer_1_out, OP_CODE
  Register_32_bits_Hold___Paralel_Load register_32_bits_hold_paralel_load_1 (
    .LOAD(MAR_C), .nPRE({32{1'b1}}), .Entrada(multiplexer_3_out), .CLK(CLK),
    .Salida({register_32_bits_hold_paralel_load_1_salida, MEM_MAR[31:2]}), .nCLR(multiplexer_2_out));
  Register_32_bits_Hold___Paralel_Load register_32_bits_hold_paralel_load_2 (
    .LOAD(MDR_C), .nPRE({32{1'b1}}), .Entrada(multiplexer_3_out), .CLK(CLK),
    .Salida(register_32_bits_hold_paralel_load_2_salida), .nCLR(multiplexer_2_out));
  Register_32_bits_Hold___Paralel_Load register_32_bits_hold_paralel_load_3 (
    .LOAD(PC_C), .nPRE({32{1'b1}}), .Entrada(multiplexer_3_out), .CLK(CLK), .Salida(MEM_PC));  // open: nCLR
  Register_32_bits_Hold___Paralel_Load register_32_bits_hold_paralel_load_4 (
    .LOAD(MBR_C), .nPRE({32{1'b1}}), .Entrada({{24{1'b0}}, register_8_bits_hold_paralel_load_2_salida}),
    .CLK(CLK),
    .Salida({register_32_bits_hold_paralel_load_4_salida_3, register_32_bits_hold_paralel_load_4_salida_2, register_32_bits_hold_paralel_load_4_salida, OP_CODE}),
    .nCLR(multiplexer_2_out));
  // Register_32_bits_Hold___Paralel_Load register_32_bits_hold_paralel_load_5: pin names not known; wires that end beside it: SP_C, register_32_bits_hold_paralel_load_5_p2, CLK, {32{1'b1}}, multiplexer_2_out, register_32_bits_hold_paralel_load_5_p6
  Register_32_bits_Hold___Paralel_Load register_32_bits_hold_paralel_load_6 (
    .LOAD(LV_C), .nPRE({32{1'b1}}), .Entrada(register_32_bits_hold_paralel_load_5_p2), .CLK(CLK),
    .Salida(register_32_bits_hold_paralel_load_6_salida), .nCLR(multiplexer_2_out));
  // Register_32_bits_Hold___Paralel_Load register_32_bits_hold_paralel_load_7: pin names not known; wires that end beside it: CPP_C, register_32_bits_hold_paralel_load_5_p2, CLK, {32{1'b1}}, multiplexer_2_out, register_32_bits_hold_paralel_load_7_p6
  Register_32_bits_Hold___Paralel_Load register_32_bits_hold_paralel_load_8 (
    .LOAD(TOS_C), .nPRE({32{1'b1}}), .Entrada(register_32_bits_hold_paralel_load_5_p2), .CLK(CLK),
    .Salida(register_32_bits_hold_paralel_load_8_salida), .nCLR(multiplexer_2_out));
  Register_32_bits_Hold___Paralel_Load register_32_bits_hold_paralel_load_9 (
    .LOAD(OPC_C), .nPRE({32{1'b1}}), .Entrada(register_32_bits_hold_paralel_load_5_p2), .CLK(CLK),
    .Salida(register_32_bits_hold_paralel_load_9_salida), .nCLR(multiplexer_2_out));
  Register_32_bits_Hold___Paralel_Load register_32_bits_hold_paralel_load_10 (
    .LOAD(H_C), .nPRE({32{1'b1}}), .Entrada(register_32_bits_hold_paralel_load_5_p2), .CLK(CLK),
    .Salida(register_32_bits_hold_paralel_load_10_salida), .nCLR(multiplexer_2_out));
  assign MEM_MAR = MDR_B ? register_32_bits_hold_paralel_load_2_salida : 32'bz;  // Controlled_Buffer controlled_buffer_1
  Register_8_bits_Hold___Paralel_Load register_8_bits_hold_paralel_load_2 (
    .nPRE({8{1'b1}}), .Entrada(MEM_PC[7:0]), .LOAD(PC_C),
    .Salida(register_8_bits_hold_paralel_load_2_salida), .CLK(CLK), .nCLR(multiplexer_1_out));
  MBR_EN mbr_en_1 (.in_1(OP_CODE), .Salida_Signada(MEM_MAR), .Salida_No_Signada(MEM_MAR), .MRB(MBR), .MBRU(MBRU));
  assign MEM_MAR = PC_B ? MEM_PC : 32'bz;  // Controlled_Buffer controlled_buffer_2
  assign MEM_MAR = SP_B ? register_32_bits_hold_paralel_load_5_p6 : 32'bz;  // Controlled_Buffer controlled_buffer_3
  assign MEM_MAR = LV_B ? register_32_bits_hold_paralel_load_6_salida : 32'bz;  // Controlled_Buffer controlled_buffer_4
  assign MEM_MAR = CPP_B ? register_32_bits_hold_paralel_load_7_p6 : 32'bz;  // Controlled_Buffer controlled_buffer_5
  assign MEM_MAR = TOS_B ? register_32_bits_hold_paralel_load_8_salida : 32'bz;  // Controlled_Buffer controlled_buffer_6
  assign MEM_MAR = OPC_B ? register_32_bits_hold_paralel_load_9_salida : 32'bz;  // Controlled_Buffer controlled_buffer_7
  // ALU_32_bit alu_32_bit_1: pin names not known; wires that end beside it: INVA, ENA, ENB, F[0], F[1], register_32_bits_hold_paralel_load_10_salida, MEM_MAR, INC, alu_32_bit_1_p9
  Shifter_DesplazadorIzqDer shifter_desplazadorizqder_1 (
    .Salida(register_32_bits_hold_paralel_load_5_p2), .Entrada(alu_32_bit_1_p9), .SRA1(SRA1), .SLL8(SLL8));

  assign MEM_WR = MEM_MAR;
  // also tied to GND on the sheet: {MEM_MAR[0], MEM_MAR[1]}

  // Notes on the sheet:
  //   Clear 8 Bits
  //   AGREGUÉ MBR: CONSULTAR
  //   Preset 32 Bits
  //   Clear 32 Bits
  //   Preset 8 Bits
  //   Preset
  //   Preset
  //   Preset
  //   Preset
  //   Preset
  //   Preset
  //   Preset
  //   Preset
  //   Preset
  //   Preset
  //   Preset
  //   Clear
  //   Clear
  //   Clear
  //   Clear
  //   Clear
  //   Clear
  //   Clear
  //   Clear
  //   Clear
  //   Clear
  //   Bus C
  //   A
  //   B
  //   Bus C
  //   Bus B
  //   Bus B
endmodule

module Register_32_bits_Hold___Paralel_Load (
  input  [31:0] nPRE,
  input  [31:0] Entrada,
  input  LOAD,
  input  CLK,
  input  [31:0] nCLR,
  output [31:0] Salida
);

  wire [31:0] multiplexer_1_out;

  Multiplexer #(.width(32), .enable("false")) multiplexer_1 (
    .in1(Entrada), .out(multiplexer_1_out), .sel(LOAD));  // open: in0
  D_FlipFlop_Des d_flipflop_des_1 (
    .D(multiplexer_1_out[31]), .CLK(CLK), .Q(Salida[31]), .nPRE(nPRE[31]), .nCLR(nCLR[31]));  // open: nQ
  D_FlipFlop_Des d_flipflop_des_2 (
    .D(multiplexer_1_out[30]), .CLK(CLK), .Q(Salida[30]), .nPRE(nPRE[30]), .nCLR(nCLR[30]));  // open: nQ
  D_FlipFlop_Des d_flipflop_des_3 (
    .D(multiplexer_1_out[29]), .CLK(CLK), .Q(Salida[29]), .nPRE(nPRE[29]), .nCLR(nCLR[29]));  // open: nQ
  D_FlipFlop_Des d_flipflop_des_4 (
    .D(multiplexer_1_out[28]), .CLK(CLK), .Q(Salida[28]), .nPRE(nPRE[28]), .nCLR(nCLR[28]));  // open: nQ
  D_FlipFlop_Des d_flipflop_des_5 (
    .D(multiplexer_1_out[27]), .CLK(CLK), .Q(Salida[27]), .nPRE(nPRE[27]), .nCLR(nCLR[27]));  // open: nQ
  D_FlipFlop_Des d_flipflop_des_6 (
    .D(multiplexer_1_out[26]), .CLK(CLK), .Q(Salida[26]), .nPRE(nPRE[26]), .nCLR(nCLR[26]));  // open: nQ
  D_FlipFlop_Des d_flipflop_des_7 (
    .D(multiplexer_1_out[25]), .CLK(CLK), .Q(Salida[25]), .nPRE(nPRE[25]), .nCLR(nCLR[25]));  // open: nQ
  D_FlipFlop_Des d_flipflop_des_8 (
    .D(multiplexer_1_out[24]), .CLK(CLK), .Q(Salida[24]), .nPRE(nPRE[24]), .nCLR(nCLR[24]));  // open: nQ
  D_FlipFlop_Des d_flipflop_des_9 (
    .D(multiplexer_1_out[23]), .CLK(CLK), .Q(Salida[23]), .nPRE(nPRE[23]), .nCLR(nCLR[23]));  // open: nQ
  D_FlipFlop_Des d_flipflop_des_10 (
    .D(multiplexer_1_out[22]), .CLK(CLK), .Q(Salida[22]), .nPRE(nPRE[22]), .nCLR(nCLR[22]));  // open: nQ
  D_FlipFlop_Des d_flipflop_des_11 (
    .D(multiplexer_1_out[21]), .CLK(CLK), .Q(Salida[21]), .nPRE(nPRE[21]), .nCLR(nCLR[21]));  // open: nQ
  D_FlipFlop_Des d_flipflop_des_12 (
    .D(multiplexer_1_out[20]), .CLK(CLK), .Q(Salida[20]), .nPRE(nPRE[20]), .nCLR(nCLR[20]));  // open: nQ
  D_FlipFlop_Des d_flipflop_des_13 (
    .D(multiplexer_1_out[19]), .CLK(CLK), .Q(Salida[19]), .nPRE(nPRE[19]), .nCLR(nCLR[19]));  // open: nQ
  D_FlipFlop_Des d_flipflop_des_14 (
    .D(multiplexer_1_out[18]), .CLK(CLK), .Q(Salida[18]), .nPRE(nPRE[18]), .nCLR(nCLR[18]));  // open: nQ
  D_FlipFlop_Des d_flipflop_des_15 (
    .D(multiplexer_1_out[17]), .CLK(CLK), .Q(Salida[17]), .nPRE(nPRE[17]), .nCLR(nCLR[17]));  // open: nQ
  D_FlipFlop_Des d_flipflop_des_16 (
    .D(multiplexer_1_out[16]), .CLK(CLK), .Q(Salida[16]), .nPRE(nPRE[16]), .nCLR(nCLR[16]));  // open: nQ
  D_FlipFlop_Des d_flipflop_des_17 (
    .D(multiplexer_1_out[15]), .CLK(CLK), .Q(Salida[15]), .nPRE(nPRE[15]), .nCLR(nCLR[15]));  // open: nQ
  D_FlipFlop_Des d_flipflop_des_18 (
    .D(multiplexer_1_out[14]), .CLK(CLK), .Q(Salida[14]), .nPRE(nPRE[14]), .nCLR(nCLR[14]));  // open: nQ
  D_FlipFlop_Des d_flipflop_des_19 (
    .D(multiplexer_1_out[13]), .CLK(CLK), .Q(Salida[13]), .nPRE(nPRE[13]), .nCLR(nCLR[13]));  // open: nQ
  D_FlipFlop_Des d_flipflop_des_20 (
    .D(multiplexer_1_out[12]), .CLK(CLK), .Q(Salida[12]), .nPRE(nPRE[12]), .nCLR(nCLR[12]));  // open: nQ
  D_FlipFlop_Des d_flipflop_des_21 (
    .D(multiplexer_1_out[11]), .CLK(CLK), .Q(Salida[11]), .nPRE(nPRE[11]), .nCLR(nCLR[11]));  // open: nQ
  D_FlipFlop_Des d_flipflop_des_22 (
    .D(multiplexer_1_out[10]), .CLK(CLK), .Q(Salida[10]), .nPRE(nPRE[10]), .nCLR(nCLR[10]));  // open: nQ
  D_FlipFlop_Des d_flipflop_des_23 (
    .D(multiplexer_1_out[9]), .CLK(CLK), .Q(Salida[9]), .nPRE(nPRE[9]), .nCLR(nCLR[9]));  // open: nQ
  D_FlipFlop_Des d_flipflop_des_24 (
    .D(multiplexer_1_out[8]), .CLK(CLK), .Q(Salida[8]), .nPRE(nPRE[8]), .nCLR(nCLR[8]));  // open: nQ
  D_FlipFlop_Des d_flipflop_des_25 (
    .D(multiplexer_1_out[7]), .CLK(CLK), .Q(Salida[7]), .nPRE(nPRE[7]), .nCLR(nCLR[7]));  // open: nQ
  D_FlipFlop_Des d_flipflop_des_26 (
    .D(multiplexer_1_out[6]), .CLK(CLK), .Q(Salida[6]), .nPRE(nPRE[6]), .nCLR(nCLR[6]));  // open: nQ
  D_FlipFlop_Des d_flipflop_des_27 (
    .D(multiplexer_1_out[5]), .CLK(CLK), .Q(Salida[5]), .nPRE(nPRE[5]), .nCLR(nCLR[5]));  // open: nQ
  D_FlipFlop_Des d_flipflop_des_28 (
    .D(multiplexer_1_out[4]), .CLK(CLK), .Q(Salida[4]), .nPRE(nPRE[4]), .nCLR(nCLR[4]));  // open: nQ
  D_FlipFlop_Des d_flipflop_des_29 (
    .D(multiplexer_1_out[3]), .CLK(CLK), .Q(Salida[3]), .nPRE(nPRE[3]), .nCLR(nCLR[3]));  // open: nQ
  D_FlipFlop_Des d_flipflop_des_30 (
    .D(multiplexer_1_out[2]), .CLK(CLK), .Q(Salida[2]), .nPRE(nPRE[2]), .nCLR(nCLR[2]));  // open: nQ
  D_FlipFlop_Des d_flipflop_des_31 (
    .D(multiplexer_1_out[1]), .CLK(CLK), .Q(Salida[1]), .nPRE(nPRE[1]), .nCLR(nCLR[1]));  // open: nQ
  D_FlipFlop_Des d_flipflop_des_32 (
    .D(multiplexer_1_out[0]), .CLK(CLK), .Q(Salida[0]), .nPRE(nPRE[0]), .nCLR(nCLR[0]));  // open: nQ
endmodule

module Register_32_bits_Des (
  input  [31:0] nPRE,
  input  [31:0] Entrada,
  input  CLK,
  input  [31:0] nCLR,
  output [31:0] Salida
);

  D_FlipFlop_Des d_flipflop_des_1 (
    .D(Entrada[31]), .CLK(CLK), .Q(Salida[31]), .nPRE(nPRE[31]), .nCLR(nCLR[31]));  // open: nQ
  D_FlipFlop_Des d_flipflop_des_2 (
    .D(Entrada[30]), .CLK(CLK), .Q(Salida[30]), .nPRE(nPRE[30]), .nCLR(nCLR[30]));  // open: nQ
  D_FlipFlop_Des d_flipflop_des_3 (
    .D(Entrada[29]), .CLK(CLK), .Q(Salida[29]), .nPRE(nPRE[29]), .nCLR(nCLR[29]));  // open: nQ
  D_FlipFlop_Des d_flipflop_des_4 (
    .D(Entrada[28]), .CLK(CLK), .Q(Salida[28]), .nPRE(nPRE[28]), .nCLR(nCLR[28]));  // open: nQ
  D_FlipFlop_Des d_flipflop_des_5 (
    .D(Entrada[27]), .CLK(CLK), .Q(Salida[27]), .nPRE(nPRE[27]), .nCLR(nCLR[27]));  // open: nQ
  D_FlipFlop_Des d_flipflop_des_6 (
    .D(Entrada[26]), .CLK(CLK), .Q(Salida[26]), .nPRE(nPRE[26]), .nCLR(nCLR[26]));  // open: nQ
  D_FlipFlop_Des d_flipflop_des_7 (
    .D(Entrada[25]), .CLK(CLK), .Q(Salida[25]), .nPRE(nPRE[25]), .nCLR(nCLR[25]));  // open: nQ
  D_FlipFlop_Des d_flipflop_des_8 (
    .D(Entrada[24]), .CLK(CLK), .Q(Salida[24]), .nPRE(nPRE[24]), .nCLR(nCLR[24]));  // open: nQ
  D_FlipFlop_Des d_flipflop_des_9 (
    .D(Entrada[23]), .CLK(CLK), .Q(Salida[23]), .nPRE(nPRE[23]), .nCLR(nCLR[23]));  // open: nQ
  D_FlipFlop_Des d_flipflop_des_10 (
    .D(Entrada[22]), .CLK(CLK), .Q(Salida[22]), .nPRE(nPRE[22]), .nCLR(nCLR[22]));  // open: nQ
  D_FlipFlop_Des d_flipflop_des_11 (
    .D(Entrada[21]), .CLK(CLK), .Q(Salida[21]), .nPRE(nPRE[21]), .nCLR(nCLR[21]));  // open: nQ
  D_FlipFlop_Des d_flipflop_des_12 (
    .D(Entrada[20]), .CLK(CLK), .Q(Salida[20]), .nPRE(nPRE[20]), .nCLR(nCLR[20]));  // open: nQ
  D_FlipFlop_Des d_flipflop_des_13 (
    .D(Entrada[19]), .CLK(CLK), .Q(Salida[19]), .nPRE(nPRE[19]), .nCLR(nCLR[19]));  // open: nQ
  D_FlipFlop_Des d_flipflop_des_14 (
    .D(Entrada[18]), .CLK(CLK), .Q(Salida[18]), .nPRE(nPRE[18]), .nCLR(nCLR[18]));  // open: nQ
  D_FlipFlop_Des d_flipflop_des_15 (
    .D(Entrada[17]), .CLK(CLK), .Q(Salida[17]), .nPRE(nPRE[17]), .nCLR(nCLR[17]));  // open: nQ
  D_FlipFlop_Des d_flipflop_des_16 (
    .D(Entrada[16]), .CLK(CLK), .Q(Salida[16]), .nPRE(nPRE[16]), .nCLR(nCLR[16]));  // open: nQ
  D_FlipFlop_Des d_flipflop_des_17 (
    .D(Entrada[15]), .CLK(CLK), .Q(Salida[15]), .nPRE(nPRE[15]), .nCLR(nCLR[15]));  // open: nQ
  D_FlipFlop_Des d_flipflop_des_18 (
    .D(Entrada[14]), .CLK(CLK), .Q(Salida[14]), .nPRE(nPRE[14]), .nCLR(nCLR[14]));  // open: nQ
  D_FlipFlop_Des d_flipflop_des_19 (
    .D(Entrada[13]), .CLK(CLK), .Q(Salida[13]), .nPRE(nPRE[13]), .nCLR(nCLR[13]));  // open: nQ
  D_FlipFlop_Des d_flipflop_des_20 (
    .D(Entrada[12]), .CLK(CLK), .Q(Salida[12]), .nPRE(nPRE[12]), .nCLR(nCLR[12]));  // open: nQ
  D_FlipFlop_Des d_flipflop_des_21 (
    .D(Entrada[11]), .CLK(CLK), .Q(Salida[11]), .nPRE(nPRE[11]), .nCLR(nCLR[11]));  // open: nQ
  D_FlipFlop_Des d_flipflop_des_22 (
    .D(Entrada[10]), .CLK(CLK), .Q(Salida[10]), .nPRE(nPRE[10]), .nCLR(nCLR[10]));  // open: nQ
  D_FlipFlop_Des d_flipflop_des_23 (
    .D(Entrada[9]), .CLK(CLK), .Q(Salida[9]), .nPRE(nPRE[9]), .nCLR(nCLR[9]));  // open: nQ
  D_FlipFlop_Des d_flipflop_des_24 (
    .D(Entrada[8]), .CLK(CLK), .Q(Salida[8]), .nPRE(nPRE[8]), .nCLR(nCLR[8]));  // open: nQ
  D_FlipFlop_Des d_flipflop_des_25 (
    .D(Entrada[7]), .CLK(CLK), .Q(Salida[7]), .nPRE(nPRE[7]), .nCLR(nCLR[7]));  // open: nQ
  D_FlipFlop_Des d_flipflop_des_26 (
    .D(Entrada[6]), .CLK(CLK), .Q(Salida[6]), .nPRE(nPRE[6]), .nCLR(nCLR[6]));  // open: nQ
  D_FlipFlop_Des d_flipflop_des_27 (
    .D(Entrada[5]), .CLK(CLK), .Q(Salida[5]), .nPRE(nPRE[5]), .nCLR(nCLR[5]));  // open: nQ
  D_FlipFlop_Des d_flipflop_des_28 (
    .D(Entrada[4]), .CLK(CLK), .Q(Salida[4]), .nPRE(nPRE[4]), .nCLR(nCLR[4]));  // open: nQ
  D_FlipFlop_Des d_flipflop_des_29 (
    .D(Entrada[3]), .CLK(CLK), .Q(Salida[3]), .nPRE(nPRE[3]), .nCLR(nCLR[3]));  // open: nQ
  D_FlipFlop_Des d_flipflop_des_30 (
    .D(Entrada[2]), .CLK(CLK), .Q(Salida[2]), .nPRE(nPRE[2]), .nCLR(nCLR[2]));  // open: nQ
  D_FlipFlop_Des d_flipflop_des_31 (
    .D(Entrada[1]), .CLK(CLK), .Q(Salida[1]), .nPRE(nPRE[1]), .nCLR(nCLR[1]));  // open: nQ
  D_FlipFlop_Des d_flipflop_des_32 (
    .D(Entrada[0]), .CLK(CLK), .Q(Salida[0]), .nPRE(nPRE[0]), .nCLR(nCLR[0]));  // open: nQ
endmodule

module Register_8_bits_Hold___Paralel_Load (
  input  [7:0] nPRE,
  input  [7:0] Entrada,
  input  LOAD,
  input  CLK,
  input  [7:0] nCLR,
  output [7:0] Salida
);

  wire [7:0] multiplexer_1_out;

  Multiplexer #(.width(8), .enable("false")) multiplexer_1 (
    .in1(Entrada), .out(multiplexer_1_out), .sel(LOAD));  // open: in0
  D_FlipFlop_Des d_flipflop_des_1 (
    .D(multiplexer_1_out[0]), .CLK(CLK), .Q(Salida[0]), .nPRE(nPRE[0]), .nCLR(nCLR[0]));  // open: nQ
  D_FlipFlop_Des d_flipflop_des_2 (
    .D(multiplexer_1_out[1]), .CLK(CLK), .Q(Salida[1]), .nPRE(nPRE[1]), .nCLR(nCLR[1]));  // open: nQ
  D_FlipFlop_Des d_flipflop_des_3 (
    .D(multiplexer_1_out[2]), .CLK(CLK), .Q(Salida[2]), .nPRE(nPRE[2]), .nCLR(nCLR[2]));  // open: nQ
  D_FlipFlop_Des d_flipflop_des_4 (
    .D(multiplexer_1_out[3]), .CLK(CLK), .Q(Salida[3]), .nPRE(nPRE[3]), .nCLR(nCLR[3]));  // open: nQ
  D_FlipFlop_Des d_flipflop_des_5 (
    .D(multiplexer_1_out[4]), .CLK(CLK), .Q(Salida[4]), .nPRE(nPRE[4]), .nCLR(nCLR[4]));  // open: nQ
  D_FlipFlop_Des d_flipflop_des_6 (
    .D(multiplexer_1_out[5]), .CLK(CLK), .Q(Salida[5]), .nPRE(nPRE[5]), .nCLR(nCLR[5]));  // open: nQ
  D_FlipFlop_Des d_flipflop_des_7 (
    .D(multiplexer_1_out[6]), .CLK(CLK), .Q(Salida[6]), .nPRE(nPRE[6]), .nCLR(nCLR[6]));  // open: nQ
  D_FlipFlop_Des d_flipflop_des_8 (
    .D(multiplexer_1_out[7]), .CLK(CLK), .Q(Salida[7]), .nPRE(nPRE[7]), .nCLR(nCLR[7]));  // open: nQ
endmodule

module Register_4_bits_Des (
  input  [3:0] nPRE,
  input  [3:0] Entrada,
  input  CLK,
  input  [3:0] nCLR,
  output [3:0] Salida
);

  D_FlipFlop_Des d_flipflop_des_1 (
    .D(Entrada[3]), .CLK(CLK), .Q(Salida[3]), .nPRE(nPRE[3]), .nCLR(nCLR[3]));  // open: nQ
  D_FlipFlop_Des d_flipflop_des_2 (
    .D(Entrada[2]), .CLK(CLK), .Q(Salida[2]), .nPRE(nPRE[2]), .nCLR(nCLR[2]));  // open: nQ
  D_FlipFlop_Des d_flipflop_des_3 (
    .D(Entrada[1]), .CLK(CLK), .Q(Salida[1]), .nPRE(nPRE[1]), .nCLR(nCLR[1]));  // open: nQ
  D_FlipFlop_Des d_flipflop_des_4 (
    .D(Entrada[0]), .CLK(CLK), .Q(Salida[0]), .nPRE(nPRE[0]), .nCLR(nCLR[0]));  // open: nQ
endmodule

module MBR_EN (
  input  [7:0] in_1,
  input  MRB,
  input  MBRU,
  output [31:0] Salida_Signada,
  output [31:0] Salida_No_Signada
);

  assign Salida_Signada = MRB ? {{25{in_1[7]}}, in_1[6:0]} : 32'bz;  // Controlled_Buffer controlled_buffer_1
  assign Salida_No_Signada = MBRU ? {{24{1'b0}}, in_1} : 32'bz;  // Controlled_Buffer controlled_buffer_2
endmodule

module D_FlipFlop_Des (
  input  nPRE,
  input  D,
  input  CLK,
  input  nCLR,
  output Q,
  output nQ
);

  wire d_latch_1_nq, not_1_out;

  D_Latch d_latch_1 (.nPRE(nPRE), .D(D), .CLK(CLK), .nQ(d_latch_1_nq), .nCLR(nCLR));  // open: Q
  not not_1 (not_1_out, CLK);
  D_Latch d_latch_2 (.nPRE(nPRE), .D(d_latch_1_nq), .Q(Q), .CLK(not_1_out), .nQ(nQ), .nCLR(nCLR));
endmodule

module D_FlipFlop_Asc (
  input  nPRE,
  input  D,
  input  CLK,
  input  nCLR,
  output Q,
  output nQ
);

  wire d_latch_1_nq, not_1_out;

  not not_1 (not_1_out, CLK);
  D_Latch d_latch_1 (.nPRE(nPRE), .D(D), .CLK(not_1_out), .nQ(d_latch_1_nq), .nCLR(nCLR));  // open: Q
  D_Latch d_latch_2 (.nPRE(nPRE), .D(d_latch_1_nq), .Q(Q), .CLK(CLK), .nQ(nQ), .nCLR(nCLR));
endmodule

module D_Latch (
  input  nPRE,
  input  D,
  input  CLK,
  input  nCLR,
  output Q,
  output nQ
);

  wire and_1_out, and_2_out, nand_1_out, nand_2_out, not_1_out;

  not not_1 (not_1_out, D);
  nand nand_1 (nand_1_out, D, CLK);
  nand nand_2 (nand_2_out, CLK, not_1_out);
  and and_1 (and_1_out, nPRE, nand_1_out);
  and and_2 (and_2_out, nand_2_out, nCLR);
  nand nand_3 (Q, and_1_out, nQ);
  nand nand_4 (nQ, Q, and_2_out);
endmodule

module ALU_1_bit (
  input  Cin,
  input  INVA,
  input  A,
  input  ENA,
  input  B,
  input  ENB,
  input  F0,
  input  F1,
  output Suma,
  output Cout
);

  wire and_1_out, and_2_out, and_3_out, and_4_out, and_5_out, and_6_out, not_1_out, not_2_out, not_3_out,
       not_4_out, sumador_completo_alu_1_s, unidad_logica_alu_1_and, unidad_logica_alu_1_not,
       unidad_logica_alu_1_or, xor_1_out;

  and and_1 (and_1_out, A, ENA);
  and and_2 (and_2_out, B, ENB);
  not not_1 (not_1_out, F0);
  not not_2 (not_2_out, F1);
  not not_3 (not_3_out, F0);
  not not_4 (not_4_out, F1);
  xor xor_1 (xor_1_out, INVA, and_1_out);
  and and_3 (and_3_out, not_1_out, not_2_out);
  and and_4 (and_4_out, not_3_out, F1);
  and and_5 (and_5_out, F0, not_4_out);
  and and_6 (and_6_out, F0, F1);
  Unidad_Logica__ALU unidad_logica_alu_1 (
    .A(xor_1_out), .B(and_2_out), .EN1(and_3_out), .EN2(and_4_out), .EN3(and_5_out),
    .AND(unidad_logica_alu_1_and), .OR(unidad_logica_alu_1_or), .NOT(unidad_logica_alu_1_not));
  Sumador_Completo__ALU sumador_completo_alu_1 (
    .Cin(Cin), .A(and_2_out), .S(sumador_completo_alu_1_s), .B(xor_1_out), .EN(and_6_out), .Cout(Cout));
  or or_1 (Suma, unidad_logica_alu_1_and, unidad_logica_alu_1_or, unidad_logica_alu_1_not, sumador_completo_alu_1_s);
endmodule

module ALU_2_bit (
  input  Carry_in,
  input  INVA,
  input  A0,
  input  ENA,
  input  B0,
  input  ENB,
  input  F0,
  input  F1,
  input  A1,
  input  B1,
  output \output ,
  output output_2,
  output Carry_Out
);

  wire alu_1_bit_1_cout;

  ALU_1_bit alu_1_bit_1 (
    .Cin(Carry_in), .INVA(INVA), .A(A0), .Suma(\output ), .ENA(ENA), .B(B0), .ENB(ENB), .F0(F0), .F1(F1),
    .Cout(alu_1_bit_1_cout));
  ALU_1_bit alu_1_bit_2 (
    .Cin(alu_1_bit_1_cout), .INVA(INVA), .A(A1), .Suma(output_2), .ENA(ENA), .B(B1), .ENB(ENB), .F0(F0),
    .F1(F1), .Cout(Carry_Out));
endmodule

module ALU_4_bit (
  input  Carry_in,
  input  INVA,
  input  A0,
  input  ENA,
  input  B0,
  input  ENB,
  input  F0,
  input  F1,
  input  A1,
  input  B1,
  input  A2,
  input  B2,
  input  A3,
  input  B3,
  output \output ,
  output output_2,
  output output_3,
  output output_4,
  output Carry_Out
);

  wire alu_2_bit_1_carry_out;

  ALU_2_bit alu_2_bit_1 (
    .INVA(INVA), .A0(A0), .ENA(ENA), .B0(B0), .ENB(ENB), .F0(F0), .F1(F1), .A1(A1), .B1(B1),
    .\output (\output ), .output_2(output_2), .Carry_Out(alu_2_bit_1_carry_out), .Carry_in(Carry_in));
  ALU_2_bit alu_2_bit_2 (
    .INVA(INVA), .A0(A2), .ENA(ENA), .B0(B2), .ENB(ENB), .F0(F0), .F1(F1), .A1(A3), .B1(B3),
    .\output (output_3), .output_2(output_4), .Carry_Out(Carry_Out), .Carry_in(alu_2_bit_1_carry_out));
endmodule

// ALU 8 bits
module ALU_8_bit (
  input  Carry_in,
  input  INVA,
  input  A0,
  input  ENA,
  input  B0,
  input  ENB,
  input  F0,
  input  F1,
  input  A1,
  input  B1,
  input  A2,
  input  B2,
  input  A3,
  input  B3,
  input  A4,
  input  B4,
  input  A5,
  input  B5,
  input  A6,
  input  B6,
  input  A7,
  input  B7,
  output \output ,
  output output_2,
  output output_3,
  output output_4,
  output output_5,
  output output_6,
  output output_7,
  output output_8,
  output Carry_Out
);

  wire alu_4_bit_1_carry_out;

  ALU_4_bit alu_4_bit_1 (
    .INVA(INVA), .A0(A0), .ENA(ENA), .B0(B0), .ENB(ENB), .F0(F0), .F1(F1), .A1(A1), .B1(B1), .A2(A2),
    .B2(B2), .A3(A3), .B3(B3), .\output (\output ), .output_2(output_2), .output_3(output_3),
    .output_4(output_4), .Carry_Out(alu_4_bit_1_carry_out), .Carry_in(Carry_in));
  ALU_4_bit alu_4_bit_2 (
    .INVA(INVA), .A0(A4), .ENA(ENA), .B0(B4), .ENB(ENB), .F0(F0), .F1(F1), .A1(A5), .B1(B5), .A2(A6),
    .B2(B6), .A3(A7), .B3(B7), .\output (output_5), .output_2(output_6), .output_3(output_7),
    .output_4(output_8), .Carry_Out(Carry_Out), .Carry_in(alu_4_bit_1_carry_out));
endmodule

module ALU_16_bit (
  input  Carry_in,
  input  INVA,
  input  A0,
  input  ENA,
  input  B0,
  input  ENB,
  input  F0,
  input  F1,
  input  A1,
  input  B1,
  input  A2,
  input  B2,
  input  A3,
  input  B3,
  input  A4,
  input  B4,
  input  A5,
  input  B5,
  input  A6,
  input  B6,
  input  A7,
  input  B7,
  input  A8,
  input  B8,
  input  A9,
  input  B9,
  input  A10,
  input  B10,
  input  A11,
  input  B11,
  input  A12,
  input  B12,
  input  A13,
  input  B13,
  input  A14,
  input  B14,
  input  A15,
  input  B15,
  output \output ,
  output output_2,
  output output_3,
  output output_4,
  output output_5,
  output output_6,
  output output_7,
  output output_8,
  output output_9,
  output output_10,
  output output_11,
  output output_12,
  output output_13,
  output output_14,
  output output_15,
  output output_16,
  output Carry_Out
);

  wire alu_8_bit_1_carry_out;

  ALU_8_bit alu_8_bit_1 (
    .INVA(INVA), .A0(A0), .ENA(ENA), .B0(B0), .ENB(ENB), .F0(F0), .F1(F1), .A1(A1), .B1(B1), .A2(A2),
    .B2(B2), .A3(A3), .B3(B3), .A4(A4), .B4(B4), .A5(A5), .B5(B5), .A6(A6), .B6(B6), .A7(A7), .B7(B7),
    .Carry_Out(alu_8_bit_1_carry_out), .Carry_in(Carry_in), .output_6(output_2), .output_7(output_3),
    .output_8(output_4), .output_5(\output ), .\output (output_5), .output_2(output_6), .output_3(output_7),
    .output_4(output_8));
  ALU_8_bit alu_8_bit_2 (
    .INVA(INVA), .A0(A8), .ENA(ENA), .B0(B8), .ENB(ENB), .F0(F0), .F1(F1), .A1(A9), .B1(B9), .A2(A10),
    .B2(B10), .A3(A11), .B3(B11), .A4(A12), .B4(B12), .A5(A13), .B5(B13), .A6(A14), .B6(B14), .A7(A15),
    .B7(B15), .Carry_Out(Carry_Out), .Carry_in(alu_8_bit_1_carry_out), .output_6(output_10),
    .output_7(output_11), .output_8(output_12), .output_5(output_9), .\output (output_13),
    .output_2(output_14), .output_3(output_15), .output_4(output_16));
endmodule

// ALU 32 bits
module ALU_32_bit (
  input  Carry_in,
  input  INVA,
  input  ENA,
  input  ENB,
  input  F0,
  input  F1,
  input  [31:0] A,
  input  [31:0] B,
  output [31:0] Salida,
  output Carry_Out
);

  wire alu_16_bit_1_carry_out;

  ALU_16_bit alu_16_bit_1 (
    .INVA(INVA), .A0(A[0]), .ENA(ENA), .B0(B[0]), .ENB(ENB), .F0(F0), .F1(F1), .A1(A[1]), .B1(B[1]),
    .A2(A[2]), .B2(B[2]), .A3(A[3]), .B3(B[3]), .A4(A[4]), .B4(B[4]), .A5(A[5]), .B5(B[5]), .A6(A[6]),
    .B6(B[6]), .A7(A[7]), .B7(B[7]), .A8(A[8]), .B8(B[8]), .A9(A[9]), .B9(B[9]), .A10(A[10]), .B10(B[10]),
    .A11(A[11]), .B11(B[11]), .A12(A[12]), .B12(B[12]), .A13(A[13]), .B13(B[13]), .A14(A[14]), .B14(B[14]),
    .A15(A[15]), .B15(B[15]), .output_2(Salida[0]), .output_3(Salida[2]), .output_4(Salida[3]),
    .output_5(Salida[4]), .output_6(Salida[5]), .output_7(Salida[6]), .Carry_Out(alu_16_bit_1_carry_out),
    .Carry_in(Carry_in), .\output (Salida[1]), .output_8(Salida[7]), .output_9(Salida[8]),
    .output_10(Salida[9]), .output_11(Salida[10]), .output_12(Salida[11]), .output_13(Salida[12]),
    .output_14(Salida[13]), .output_15(Salida[14]), .output_16(Salida[15]));
  ALU_16_bit alu_16_bit_2 (
    .INVA(INVA), .A0(A[16]), .ENA(ENA), .B0(B[16]), .ENB(ENB), .F0(F0), .F1(F1), .A1(A[17]), .B1(B[17]),
    .A2(A[18]), .B2(B[18]), .A3(A[19]), .B3(B[19]), .A4(A[20]), .B4(B[20]), .A5(A[21]), .B5(B[21]),
    .A6(A[22]), .B6(B[22]), .A7(A[23]), .B7(B[23]), .A8(A[24]), .B8(B[24]), .A9(A[25]), .B9(B[25]),
    .A10(A[26]), .B10(B[26]), .A11(A[27]), .B11(B[27]), .A12(A[28]), .B12(B[28]), .A13(A[29]), .B13(B[29]),
    .A14(A[30]), .B14(B[30]), .A15(A[31]), .B15(B[31]), .output_2(Salida[16]), .output_3(Salida[18]),
    .output_4(Salida[19]), .output_5(Salida[20]), .output_6(Salida[21]), .output_7(Salida[22]),
    .Carry_Out(Carry_Out), .Carry_in(alu_16_bit_1_carry_out), .\output (Salida[17]), .output_8(Salida[23]),
    .output_9(Salida[24]), .output_10(Salida[25]), .output_11(Salida[26]), .output_12(Salida[27]),
    .output_13(Salida[28]), .output_14(Salida[29]), .output_15(Salida[30]), .output_16(Salida[31]));
endmodule

module Unidad_Logica__ALU (
  input  A,
  input  B,
  input  EN1,
  input  EN2,
  input  EN3,
  output AND,
  output OR,
  output NOT
);

  wire and_1_out, not_1_out, or_1_out;

  and and_1 (and_1_out, A, B);
  or or_1 (or_1_out, A, B);
  not not_1 (not_1_out, B);
  and and_2 (AND, and_1_out, EN1);
  and and_3 (OR, or_1_out, EN2);
  and and_4 (NOT, not_1_out, EN3);

  // Notes on the sheet:
  //   AB
  //   A+B
  //   /B
endmodule

module Sumador_Completo__ALU (
  input  Cin,
  input  A,
  input  B,
  input  EN,
  output S,
  output Cout
);

  wire and_1_out, and_2_out, and_3_out, and_4_out, xor_1_out;

  and and_1 (and_1_out, A, EN);
  and and_2 (and_2_out, B, EN);
  and and_3 (and_3_out, and_1_out, and_2_out);
  xor xor_1 (xor_1_out, and_1_out, and_2_out);
  or or_1 (Cout, and_3_out, and_4_out);
  and and_4 (and_4_out, xor_1_out, Cin);
  xor xor_2 (S, Cin, xor_1_out);
endmodule

module Desplazador__Registro_Universal (
  input  [31:0] Entrada,
  input  CLK,
  input  Dd,
  input  Di,
  input  [1:0] Funcion,
  output Qd,
  output Qi,
  output [31:0] Salida
);

  wire multiplexer_1_out, multiplexer_2_out, multiplexer_3_out, multiplexer_4_out, multiplexer_5_out,
       multiplexer_6_out, multiplexer_7_out, multiplexer_8_out, multiplexer_9_out, multiplexer_10_out,
       multiplexer_11_out, multiplexer_12_out, multiplexer_13_out, multiplexer_14_out, multiplexer_15_out,
       multiplexer_16_out, multiplexer_17_out, multiplexer_18_out, multiplexer_19_out, multiplexer_20_out,
       multiplexer_21_out, multiplexer_22_out, multiplexer_23_out, multiplexer_24_out, multiplexer_25_out,
       multiplexer_26_out, multiplexer_27_out, multiplexer_28_out, multiplexer_29_out, multiplexer_30_out,
       multiplexer_31_out, multiplexer_32_out;

  Multiplexer #(.select(2), .enable("false")) multiplexer_1 (
    .in0(Entrada[31]), .in1(Di), .in2(Salida[30]), .in3(Qi), .out(multiplexer_1_out), .sel(Funcion));
  D_Flip_Flop d_ff_1 (.clk(CLK), .D(multiplexer_1_out), .Q(Qi));  // open: Qn, preset, en, reset
  Multiplexer #(.select(2), .enable("false")) multiplexer_2 (
    .in0(Entrada[30]), .in1(Qi), .in2(Salida[29]), .in3(Salida[30]), .out(multiplexer_2_out), .sel(Funcion));
  D_Flip_Flop d_ff_2 (.clk(CLK), .D(multiplexer_2_out), .Q(Salida[30]));  // open: Qn, preset, en, reset
  Multiplexer #(.select(2), .enable("false")) multiplexer_3 (
    .in0(Entrada[29]), .in1(Salida[30]), .in2(Salida[28]), .in3(Salida[29]), .out(multiplexer_3_out),
    .sel(Funcion));
  D_Flip_Flop d_ff_3 (.clk(CLK), .D(multiplexer_3_out), .Q(Salida[29]));  // open: Qn, preset, en, reset
  D_Flip_Flop d_ff_4 (.clk(CLK), .D(multiplexer_4_out), .Q(Salida[28]));  // open: Qn, preset, en, reset
  Multiplexer #(.select(2), .enable("false")) multiplexer_4 (
    .in0(Entrada[28]), .in1(Salida[29]), .in2(Salida[27]), .in3(Salida[28]), .out(multiplexer_4_out),
    .sel(Funcion));
  Multiplexer #(.select(2), .enable("false")) multiplexer_5 (
    .in0(Entrada[27]), .in1(Salida[28]), .in2(Salida[26]), .in3(Salida[27]), .out(multiplexer_5_out),
    .sel(Funcion));
  D_Flip_Flop d_ff_5 (.clk(CLK), .D(multiplexer_5_out), .Q(Salida[27]));  // open: Qn, preset, en, reset
  Multiplexer #(.select(2), .enable("false")) multiplexer_6 (
    .in0(Entrada[26]), .in1(Salida[27]), .in2(Salida[25]), .in3(Salida[26]), .out(multiplexer_6_out),
    .sel(Funcion));
  D_Flip_Flop d_ff_6 (.clk(CLK), .D(multiplexer_6_out), .Q(Salida[26]));  // open: Qn, preset, en, reset
  Multiplexer #(.select(2), .enable("false")) multiplexer_7 (
    .in0(Entrada[25]), .in1(Salida[26]), .in2(Salida[24]), .in3(Salida[25]), .out(multiplexer_7_out),
    .sel(Funcion));
  D_Flip_Flop d_ff_7 (.clk(CLK), .D(multiplexer_7_out), .Q(Salida[25]));  // open: Qn, preset, en, reset
  Multiplexer #(.select(2), .enable("false")) multiplexer_8 (
    .in0(Entrada[24]), .in1(Salida[25]), .in2(Salida[23]), .in3(Salida[24]), .out(multiplexer_8_out),
    .sel(Funcion));
  D_Flip_Flop d_ff_8 (.clk(CLK), .D(multiplexer_8_out), .Q(Salida[24]));  // open: Qn, preset, en, reset
  Multiplexer #(.select(2), .enable("false")) multiplexer_9 (
    .in0(Entrada[23]), .in1(Salida[24]), .in2(Salida[22]), .in3(Salida[23]), .out(multiplexer_9_out),
    .sel(Funcion));
  D_Flip_Flop d_ff_9 (.clk(CLK), .D(multiplexer_9_out), .Q(Salida[23]));  // open: Qn, preset, en, reset
  Multiplexer #(.select(2), .enable("false")) multiplexer_10 (
    .in0(Entrada[22]), .in1(Salida[23]), .in2(Salida[21]), .in3(Salida[22]), .out(multiplexer_10_out),
    .sel(Funcion));
  D_Flip_Flop d_ff_10 (.clk(CLK), .D(multiplexer_10_out), .Q(Salida[22]));  // open: Qn, preset, en, reset
  Multiplexer #(.select(2), .enable("false")) multiplexer_11 (
    .in0(Entrada[21]), .in1(Salida[22]), .in2(Salida[20]), .in3(Salida[21]), .out(multiplexer_11_out),
    .sel(Funcion));
  D_Flip_Flop d_ff_11 (.clk(CLK), .D(multiplexer_11_out), .Q(Salida[21]));  // open: Qn, preset, en, reset
  Multiplexer #(.select(2), .enable("false")) multiplexer_12 (
    .in0(Entrada[20]), .in1(Salida[21]), .in2(Salida[19]), .in3(Salida[20]), .out(multiplexer_12_out),
    .sel(Funcion));
  D_Flip_Flop d_ff_12 (.clk(CLK), .D(multiplexer_12_out), .Q(Salida[20]));  // open: Qn, preset, en, reset
  Multiplexer #(.select(2), .enable("false")) multiplexer_13 (
    .in0(Entrada[19]), .in1(Salida[20]), .in2(Salida[18]), .in3(Salida[19]), .out(multiplexer_13_out),
    .sel(Funcion));
  D_Flip_Flop d_ff_13 (.clk(CLK), .D(multiplexer_13_out), .Q(Salida[19]));  // open: Qn, preset, en, reset
  D_Flip_Flop d_ff_14 (.clk(CLK), .D(multiplexer_14_out), .Q(Salida[18]));  // open: Qn, preset, en, reset
  Multiplexer #(.select(2), .enable("false")) multiplexer_14 (
    .in0(Entrada[18]), .in1(Salida[19]), .in2(Salida[17]), .in3(Salida[18]), .out(multiplexer_14_out),
    .sel(Funcion));
  Multiplexer #(.select(2), .enable("false")) multiplexer_15 (
    .in0(Entrada[17]), .in1(Salida[18]), .in2(Salida[16]), .in3(Salida[17]), .out(multiplexer_15_out),
    .sel(Funcion));
  D_Flip_Flop d_ff_15 (.clk(CLK), .D(multiplexer_15_out), .Q(Salida[17]));  // open: Qn, preset, en, reset
  Multiplexer #(.select(2), .enable("false")) multiplexer_16 (
    .in0(Entrada[16]), .in1(Salida[17]), .in2(Salida[15]), .in3(Salida[16]), .out(multiplexer_16_out),
    .sel(Funcion));
  D_Flip_Flop d_ff_16 (.clk(CLK), .D(multiplexer_16_out), .Q(Salida[16]));  // open: Qn, preset, en, reset
  Multiplexer #(.select(2), .enable("false")) multiplexer_17 (
    .in0(Entrada[15]), .in1(Salida[16]), .in2(Salida[14]), .in3(Salida[15]), .out(multiplexer_17_out),
    .sel(Funcion));
  D_Flip_Flop d_ff_17 (.clk(CLK), .D(multiplexer_17_out), .Q(Salida[15]));  // open: Qn, preset, en, reset
  D_Flip_Flop d_ff_18 (.clk(CLK), .D(multiplexer_18_out), .Q(Salida[14]));  // open: Qn, preset, en, reset
  Multiplexer #(.select(2), .enable("false")) multiplexer_18 (
    .in0(Entrada[14]), .in1(Salida[15]), .in2(Salida[13]), .in3(Salida[14]), .out(multiplexer_18_out),
    .sel(Funcion));
  Multiplexer #(.select(2), .enable("false")) multiplexer_19 (
    .in0(Entrada[13]), .in1(Salida[14]), .in2(Salida[12]), .in3(Salida[13]), .out(multiplexer_19_out),
    .sel(Funcion));
  D_Flip_Flop d_ff_19 (.clk(CLK), .D(multiplexer_19_out), .Q(Salida[13]));  // open: Qn, preset, en, reset
  Multiplexer #(.select(2), .enable("false")) multiplexer_20 (
    .in0(Entrada[12]), .in1(Salida[13]), .in2(Salida[11]), .in3(Salida[12]), .out(multiplexer_20_out),
    .sel(Funcion));
  D_Flip_Flop d_ff_20 (.clk(CLK), .D(multiplexer_20_out), .Q(Salida[12]));  // open: Qn, preset, en, reset
  Multiplexer #(.select(2), .enable("false")) multiplexer_21 (
    .in0(Entrada[11]), .in1(Salida[12]), .in2(Salida[10]), .in3(Salida[11]), .out(multiplexer_21_out),
    .sel(Funcion));
  D_Flip_Flop d_ff_21 (.clk(CLK), .D(multiplexer_21_out), .Q(Salida[11]));  // open: Qn, preset, en, reset
  Multiplexer #(.select(2), .enable("false")) multiplexer_22 (
    .in0(Entrada[10]), .in1(Salida[11]), .in2(Salida[9]), .in3(Salida[10]), .out(multiplexer_22_out),
    .sel(Funcion));
  D_Flip_Flop d_ff_22 (.clk(CLK), .D(multiplexer_22_out), .Q(Salida[10]));  // open: Qn, preset, en, reset
  Multiplexer #(.select(2), .enable("false")) multiplexer_23 (
    .in0(Entrada[9]), .in1(Salida[10]), .in2(Salida[8]), .in3(Salida[9]), .out(multiplexer_23_out),
    .sel(Funcion));
  D_Flip_Flop d_ff_23 (.clk(CLK), .D(multiplexer_23_out), .Q(Salida[9]));  // open: Qn, preset, en, reset
  Multiplexer #(.select(2), .enable("false")) multiplexer_24 (
    .in0(Entrada[8]), .in1(Salida[9]), .in2(Salida[7]), .in3(Salida[8]), .out(multiplexer_24_out),
    .sel(Funcion));
  D_Flip_Flop d_ff_24 (.clk(CLK), .D(multiplexer_24_out), .Q(Salida[8]));  // open: Qn, preset, en, reset
  Multiplexer #(.select(2), .enable("false")) multiplexer_25 (
    .in0(Entrada[7]), .in1(Salida[8]), .in2(Salida[6]), .in3(Salida[7]), .out(multiplexer_25_out),
    .sel(Funcion));
  D_Flip_Flop d_ff_25 (.clk(CLK), .D(multiplexer_25_out), .Q(Salida[7]));  // open: Qn, preset, en, reset
  Multiplexer #(.select(2), .enable("false")) multiplexer_26 (
    .in0(Entrada[6]), .in1(Salida[7]), .in2(Salida[5]), .in3(Salida[6]), .out(multiplexer_26_out),
    .sel(Funcion));
  D_Flip_Flop d_ff_26 (.clk(CLK), .D(multiplexer_26_out), .Q(Salida[6]));  // open: Qn, preset, en, reset
  Multiplexer #(.select(2), .enable("false")) multiplexer_27 (
    .in0(Entrada[5]), .in1(Salida[6]), .in2(Salida[4]), .in3(Salida[5]), .out(multiplexer_27_out),
    .sel(Funcion));
  D_Flip_Flop d_ff_27 (.clk(CLK), .D(multiplexer_27_out), .Q(Salida[5]));  // open: Qn, preset, en, reset
  D_Flip_Flop d_ff_28 (.clk(CLK), .D(multiplexer_28_out), .Q(Salida[4]));  // open: Qn, preset, en, reset
  Multiplexer #(.select(2), .enable("false")) multiplexer_28 (
    .in0(Entrada[4]), .in1(Salida[5]), .in2(Salida[3]), .in3(Salida[4]), .out(multiplexer_28_out),
    .sel(Funcion));
  Multiplexer #(.select(2), .enable("false")) multiplexer_29 (
    .in0(Entrada[3]), .in1(Salida[4]), .in2(Salida[2]), .in3(Salida[3]), .out(multiplexer_29_out),
    .sel(Funcion));
  D_Flip_Flop d_ff_29 (.clk(CLK), .D(multiplexer_29_out), .Q(Salida[3]));  // open: Qn, preset, en, reset
  Multiplexer #(.select(2), .enable("false")) multiplexer_30 (
    .in0(Entrada[2]), .in1(Salida[3]), .in2(Salida[1]), .in3(Salida[2]), .out(multiplexer_30_out),
    .sel(Funcion));
  D_Flip_Flop d_ff_30 (.clk(CLK), .D(multiplexer_30_out), .Q(Salida[2]));  // open: Qn, preset, en, reset
  Multiplexer #(.select(2), .enable("false")) multiplexer_31 (
    .in0(Entrada[1]), .in1(Salida[2]), .in2(Qd), .in3(Salida[1]), .out(multiplexer_31_out), .sel(Funcion));
  D_Flip_Flop d_ff_31 (.clk(CLK), .D(multiplexer_31_out), .Q(Salida[1]));  // open: Qn, preset, en, reset
  Multiplexer #(.select(2), .enable("false")) multiplexer_32 (
    .in0(Entrada[0]), .in1(Salida[1]), .in2(Dd), .in3(Qd), .out(multiplexer_32_out), .sel(Funcion));
  D_Flip_Flop d_ff_32 (.clk(CLK), .D(multiplexer_32_out), .Q(Qd));  // open: Qn, preset, en, reset

  assign {Salida[31], Salida[0]} = {Qi, Qd};

  // Notes on the sheet:
  //   Catga y lectura en serie 
  //   11 Hold
  //   00 Carga en paralelo
  //   01 desplaza a la derecha
  //   10 desplaza a la izquierda
  //   Consultar si debe estar habilitada la carga en serie
endmodule

module Shifter_DesplazadoresLogisim (
  input  [31:0] Entrada,
  input  SRA1,
  input  SLL8,
  output [31:0] Salida
);

  wire and_1_out, and_2_out, and_3_out, and_4_out, not_1_out, not_2_out;
  wire [31:0] shifter_1_out, shifter_2_out;

  not not_1 (not_1_out, SLL8);
  not not_2 (not_2_out, SRA1);
  and and_1 (and_1_out, not_2_out, not_1_out);
  and and_2 (and_2_out, not_2_out, SLL8);
  and and_3 (and_3_out, SRA1, not_1_out);
  and and_4 (and_4_out, SRA1, SLL8);
  assign Salida = and_1_out ? Entrada : 32'bz;  // Controlled_Buffer controlled_buffer_1
  assign Salida = and_4_out ? Entrada : 32'bz;  // Controlled_Buffer controlled_buffer_2
  Shifter #(.width(32)) shifter_1 (.in(Entrada), .\dist (5'b01000), .out(shifter_1_out));
  Shifter #(.width(32), .shift("ar")) shifter_2 (.in(Entrada), .\dist (5'b00001), .out(shifter_2_out));
  assign Salida = and_2_out ? shifter_1_out : 32'bz;  // Controlled_Buffer controlled_buffer_3
  assign Salida = and_3_out ? shifter_2_out : 32'bz;  // Controlled_Buffer controlled_buffer_4

  // Notes on the sheet:
  //   Logical Left
  //   Arithmetic Right
endmodule

module DesplazadorDerecha_1_bit (
  input  [31:0] Entrada,
  input  C,
  output [31:0] Salida
);

  wire and_1_out, and_2_out, and_3_out, and_4_out, and_5_out, and_6_out, and_7_out, and_8_out, and_9_out,
       and_10_out, and_11_out, and_12_out, and_13_out, and_14_out, and_15_out, and_16_out, and_17_out,
       and_18_out, and_19_out, and_20_out, and_21_out, and_22_out, and_23_out, and_24_out, and_25_out,
       and_26_out, and_27_out, and_28_out, and_29_out, and_30_out, and_31_out, and_32_out, and_33_out,
       and_34_out, and_35_out, and_36_out, and_37_out, and_38_out, and_39_out, and_40_out, and_41_out,
       and_42_out, and_43_out, and_44_out, and_45_out, and_46_out, and_47_out, and_48_out, and_49_out,
       and_50_out, and_51_out, and_52_out, and_53_out, and_54_out, and_55_out, and_56_out, and_57_out,
       and_58_out, and_59_out, and_60_out, and_62_out, not_1_out, not_2_out;

  and and_1 (and_1_out, Entrada[31], not_2_out);
  and and_2 (and_2_out, not_1_out, Entrada[30]);
  or or_1 (Salida[31], and_2_out, Salida[30]);
  and and_3 (and_3_out, Entrada[30], not_2_out);
  or or_2 (Salida[30], and_1_out, and_4_out);
  and and_4 (and_4_out, not_1_out, Entrada[29]);
  and and_5 (and_5_out, Entrada[29], not_2_out);
  or or_3 (Salida[29], and_3_out, and_6_out);
  and and_6 (and_6_out, not_1_out, Entrada[28]);
  or or_4 (Salida[28], and_5_out, and_8_out);
  and and_7 (and_7_out, Entrada[28], not_2_out);
  and and_8 (and_8_out, not_1_out, Entrada[27]);
  and and_9 (and_9_out, Entrada[27], not_2_out);
  or or_5 (Salida[27], and_7_out, and_10_out);
  and and_10 (and_10_out, not_1_out, Entrada[26]);
  and and_11 (and_11_out, Entrada[26], not_2_out);
  or or_6 (Salida[26], and_9_out, and_12_out);
  and and_12 (and_12_out, not_1_out, Entrada[25]);
  and and_13 (and_13_out, Entrada[25], not_2_out);
  or or_7 (Salida[25], and_11_out, and_14_out);
  and and_14 (and_14_out, not_1_out, Entrada[24]);
  or or_8 (Salida[24], and_13_out, and_17_out);
  and and_15 (and_15_out, Entrada[24], not_2_out);
  and and_16 (and_16_out, Entrada[23], not_2_out);
  and and_17 (and_17_out, not_1_out, Entrada[23]);
  or or_9 (Salida[23], and_15_out, and_18_out);
  and and_18 (and_18_out, not_1_out, Entrada[22]);
  and and_19 (and_19_out, Entrada[22], not_2_out);
  or or_10 (Salida[22], and_16_out, and_20_out);
  and and_20 (and_20_out, not_1_out, Entrada[21]);
  and and_21 (and_21_out, Entrada[21], not_2_out);
  or or_11 (Salida[21], and_19_out, and_22_out);
  and and_22 (and_22_out, not_1_out, Entrada[20]);
  or or_12 (Salida[20], and_21_out, and_25_out);
  and and_23 (and_23_out, Entrada[20], not_2_out);
  and and_24 (and_24_out, Entrada[19], not_2_out);
  and and_25 (and_25_out, not_1_out, Entrada[19]);
  or or_13 (Salida[19], and_23_out, and_26_out);
  and and_26 (and_26_out, not_1_out, Entrada[18]);
  and and_27 (and_27_out, Entrada[18], not_2_out);
  or or_14 (Salida[18], and_24_out, and_28_out);
  and and_28 (and_28_out, not_1_out, Entrada[17]);
  or or_15 (Salida[17], and_27_out, and_30_out);
  and and_29 (and_29_out, Entrada[17], not_2_out);
  and and_30 (and_30_out, not_1_out, Entrada[16]);
  or or_16 (Salida[16], and_29_out, and_32_out);
  and and_31 (and_31_out, Entrada[16], not_2_out);
  and and_32 (and_32_out, not_1_out, Entrada[15]);
  and and_33 (and_33_out, Entrada[15], not_2_out);
  or or_17 (Salida[15], and_31_out, and_34_out);
  and and_34 (and_34_out, not_1_out, Entrada[14]);
  and and_35 (and_35_out, Entrada[14], not_2_out);
  or or_18 (Salida[14], and_33_out, and_36_out);
  and and_36 (and_36_out, not_1_out, Entrada[13]);
  or or_19 (Salida[13], and_35_out, and_38_out);
  and and_37 (and_37_out, Entrada[13], not_2_out);
  and and_38 (and_38_out, not_1_out, Entrada[12]);
  or or_20 (Salida[12], and_37_out, and_41_out);
  and and_39 (and_39_out, Entrada[12], not_2_out);
  and and_40 (and_40_out, Entrada[11], not_2_out);
  and and_41 (and_41_out, not_1_out, Entrada[11]);
  or or_21 (Salida[11], and_39_out, and_42_out);
  and and_42 (and_42_out, not_1_out, Entrada[10]);
  and and_43 (and_43_out, Entrada[10], not_2_out);
  or or_22 (Salida[10], and_40_out, and_44_out);
  and and_44 (and_44_out, not_1_out, Entrada[9]);
  or or_23 (Salida[9], and_43_out, and_46_out);
  and and_45 (and_45_out, Entrada[9], not_2_out);
  and and_46 (and_46_out, not_1_out, Entrada[8]);
  or or_24 (Salida[8], and_45_out, and_49_out);
  and and_47 (and_47_out, Entrada[8], not_2_out);
  and and_48 (and_48_out, Entrada[7], not_2_out);
  and and_49 (and_49_out, not_1_out, Entrada[7]);
  or or_25 (Salida[7], and_47_out, and_50_out);
  and and_50 (and_50_out, not_1_out, Entrada[6]);
  and and_51 (and_51_out, Entrada[6], not_2_out);
  or or_26 (Salida[6], and_48_out, and_52_out);
  and and_52 (and_52_out, not_1_out, Entrada[5]);
  or or_27 (Salida[5], and_51_out, and_55_out);
  and and_53 (and_53_out, Entrada[5], not_2_out);
  and and_54 (and_54_out, Entrada[4], not_2_out);
  and and_55 (and_55_out, not_1_out, Entrada[4]);
  or or_28 (Salida[4], and_53_out, and_56_out);
  and and_56 (and_56_out, not_1_out, Entrada[3]);
  and and_57 (and_57_out, Entrada[3], not_2_out);
  or or_29 (Salida[3], and_54_out, and_58_out);
  and and_58 (and_58_out, not_1_out, Entrada[2]);
  and and_59 (and_59_out, Entrada[2], not_2_out);
  or or_30 (Salida[2], and_57_out, and_60_out);
  and and_60 (and_60_out, not_1_out, Entrada[1]);
  or or_31 (Salida[1], and_59_out, and_62_out);
  and and_61 (Salida[0], Entrada[1], not_2_out);
  and and_62 (and_62_out, not_1_out, Entrada[0]);
  not not_1 (not_1_out, C);
  not not_2 (not_2_out, not_1_out);

  // Notes on the sheet:
  //   Sirve para conservar el valor del bit mas significativo
endmodule

module DesplazadorIzquierda_8bits (
  input  [31:0] Entrada,
  output [31:0] Salida
);


  assign Salida = {Entrada[23:0], {8{1'b0}}};
endmodule

// Shifter
module Shifter_DesplazadorIzqDer (
  input  [31:0] Entrada,
  input  SRA1,
  input  SLL8,
  output [31:0] Salida
);

  wire and_1_out, and_2_out, and_3_out, and_4_out, not_1_out, not_2_out;
  wire [31:0] desplazadorderecha_1_bit_1_salida, desplazadorizquierda_8bits_1_salida;

  not not_1 (not_1_out, SRA1);
  not not_2 (not_2_out, SLL8);
  and and_1 (and_1_out, not_1_out, not_2_out);
  and and_2 (and_2_out, not_1_out, SLL8);
  and and_3 (and_3_out, SRA1, not_2_out);
  and and_4 (and_4_out, SRA1, SLL8);
  assign Salida = and_1_out ? Entrada : 32'bz;  // Controlled_Buffer controlled_buffer_1
  DesplazadorIzquierda_8bits desplazadorizquierda_8bits_1 (
    .Entrada(Entrada), .Salida(desplazadorizquierda_8bits_1_salida));
  assign Salida = and_4_out ? Entrada : 32'bz;  // Controlled_Buffer controlled_buffer_2
  DesplazadorDerecha_1_bit desplazadorderecha_1_bit_1 (
    .Entrada(Entrada), .C(and_3_out), .Salida(desplazadorderecha_1_bit_1_salida));
  assign Salida = and_2_out ? desplazadorizquierda_8bits_1_salida : 32'bz;  // Controlled_Buffer controlled_buffer_3
  assign Salida = and_3_out ? desplazadorderecha_1_bit_1_salida : 32'bz;  // Controlled_Buffer controlled_buffer_4

  // Notes on the sheet:
  //   DEMULTIPLEXOR
  //   8 bits
  //   1 bit
endmodule
